# Fritzing sketch Reaktionstester_V1_0 (saved by Fritzing 0.9.2b)
circuit board: 8.46667cm x 5.64444cm
breadboards: 1

parts:
  R1 = Resistor [tolerance=±5% resistance=220 package=THT]
  LED1 = LED - 5mm [color="Red (633nm)" package="5 mm [THT]"]
  LCD1 = LCD screen
  S1 = Pushbutton [package="[THT]"]
  Bauteil1 = Arduino Uno (Rev3)
  R2 = Resistor [tolerance=±5% resistance=1k package=THT]

nets:
  N1: R1.Pin_0, LED1.anode
  N2: R1.Pin_1, Bauteil1.D10_PWM/SS
  VSS: LED1.cathode, LCD1.VSS, LCD1.LED-, Bauteil1.GND, R2.Pin_0
  VDD: LCD1.VDD, LCD1.LED+, S1.Pin_3, S1.Pin_4, Bauteil1.D9_PWM, Bauteil1.5V, R2.Pin_1
  N3: LCD1.E, Bauteil1.D2
  N4: LCD1.DB4, Bauteil1.D4
  N5: LCD1.DB5, Bauteil1.D5_PWM
  N6: LCD1.DB6, Bauteil1.D6_PWM
  N7: LCD1.DB7, Bauteil1.D7
  N8: S1.Pin_1, S1.Pin_2
